# Fritzing sketch Aaron_Circuit (saved by Fritzing 1.0.0rc)
breadboards: 1

parts:
  Brain = Arduino Uno (Rev3)
  Driver_Limbs = 16-Channel 12-bit PWM Servo Driver - I2C [part_number=815]
  J2 = Basic Servo [part_number=MG996R]
  F2 = Resettable Fuse PTC [part_number=RKEF075-2 package=ptc]
  J3 = Basic Servo [part_number=MG996R]
  F3 = Resettable Fuse PTC [part_number=RKEF075-2 package=ptc]
  J4 = Basic Servo [part_number=MG996R]
  F4 = Resettable Fuse PTC [part_number=RKEF075-2 package=ptc]
  J5 = Basic Servo [part_number=MG996R]
  F5 = Resettable Fuse PTC [part_number=RKEF075-2 package=ptc]
  J6 = Basic Servo [part_number=MG996R]
  F6 = Resettable Fuse PTC [part_number=RKEF075-2 package=ptc]
  J7 = Basic Servo [part_number=MG996R]
  F7 = Resettable Fuse PTC [part_number=RKEF075-2 package=ptc]
  J8 = Basic Servo [part_number=MG996R]
  F8 = Resettable Fuse PTC [part_number=RKEF075-2 package=ptc]
  J9 = Basic Servo [part_number=MG996R]
  F9 = Resettable Fuse PTC [part_number=RKEF075-2 package=ptc]
  S3 = Pushbutton [package="[THT]"]
  S4 = Pushbutton [package="[THT]"]
  Eye_R = NeoPixel NeoMatrix 8x8 [part_number=1487]
  Eye_L = NeoPixel NeoMatrix 8x8 [part_number=1487]
  D8 = Rectifier Diode [part_number=1N4001 package="300 mil [THT]"]
  D9 = Zener Diode [part_number=1N4732A breakdown_voltage=3.6V package="Melf DO-213 AB [SMD]"]
  Q3 = NPN-Transistor [part_number=BC547CBU-ND package="TO92 [THT]"]
  U3 = RELAY [part_number=PR9-5V-200-1A package=relay-g5q]
  R3 = Resistor [tolerance=±5% power=0.25W resistance=10k package=THT]
  R4 = Resistor [tolerance=±5% resistance=1k power=0.25W package=THT]
  D10 = Schottky Diode [part_number=15SQ100 package="300 mil [THT]"]
  D11 = Rectifier Diode [part_number=1N4001 package="300 mil [THT]"]
  D12 = Zener Diode [part_number=1N4732A breakdown_voltage=3.6V package="Melf DO-213 AB [SMD]"]
  D13 = Schottky Diode [part_number=15SQ100 package="300 mil [THT]"]
  Q4 = NPN-Transistor [part_number=BC547CBU-ND package="TO92 [THT]"]
  U4 = RELAY [part_number=PR9-5V-200-1A package=relay-g5q]
  C2 = Electrolytic Capacitor [capacitance=1mF voltage=16V package="100 mil [THT, electrolytic]"]
  PWR_Supply = Power plug
  J15 = Basic Servo [part_number=MG996R]
  F15 = Resettable Fuse PTC [part_number=RKEF075-2 package=ptc]
  D14 = Rectifier Diode [part_number=1N4001 package="300 mil [THT]"]
  D15 = Rectifier Diode [part_number=1N4001 package="300 mil [THT]"]
  D16 = Zener Diode [part_number=1N4732A breakdown_voltage=3.6V package="Melf DO-213 AB [SMD]"]
  D17 = Zener Diode [part_number=1N4732A breakdown_voltage=3.6V package="Melf DO-213 AB [SMD]"]
  J16 = Basic Servo [part_number=MG996R]
  F16 = Resettable Fuse PTC [part_number=RKEF075-2 package=ptc]
  J17 = Basic Servo [part_number=MG996R]
  F17 = Resettable Fuse PTC [part_number=RKEF075-2 package=ptc]
  J18 = Basic Servo [part_number=MG996R]
  F18 = Resettable Fuse PTC [part_number=RKEF075-2 package=ptc]
  J19 = Basic Servo [part_number=MG996R]
  F19 = Resettable Fuse PTC [part_number=RKEF075-2 package=ptc]
  J20 = Basic Servo [part_number=MG996R]
  F20 = Resettable Fuse PTC [part_number=RKEF075-2 package=ptc]
  J21 = Basic Servo [part_number=MG996R]
  F21 = Resettable Fuse PTC [part_number=RKEF075-2 package=ptc]
  J22 = Basic Servo [part_number=MG996R]
  F22 = Resettable Fuse PTC [part_number=RKEF075-2 package=ptc]
  D18 = Schottky Diode [part_number=15SQ100 package="300 mil [THT]"]
  D19 = Schottky Diode [part_number=15SQ100 package="300 mil [THT]"]
  Q5 = NPN-Transistor [part_number=BC547CBU-ND package="TO92 [THT]"]
  Q6 = NPN-Transistor [part_number=BC547CBU-ND package="TO92 [THT]"]
  U5 = RELAY [part_number=PR9-5V-200-1A package=relay-g5q]
  U6 = RELAY [part_number=PR9-5V-200-1A package=relay-g5q]
  Driver_Limbs1 = 16-Channel 12-bit PWM Servo Driver - I2C [part_number=815]
  J24 = Basic Servo [part_number=MG996R]
  F24 = Resettable Fuse PTC [part_number=RKEF075-2 package=ptc]
  D21 = Rectifier Diode [part_number=1N4001 package="300 mil [THT]"]
  D23 = Rectifier Diode [part_number=1N4001 package="300 mil [THT]"]
  D26 = Zener Diode [part_number=1N4732A breakdown_voltage=3.6V package="Melf DO-213 AB [SMD]"]
  D27 = Zener Diode [part_number=1N4732A breakdown_voltage=3.6V package="Melf DO-213 AB [SMD]"]
  J26 = Basic Servo [part_number=MG996R]
  F26 = Resettable Fuse PTC [part_number=RKEF075-2 package=ptc]
  J28 = Basic Servo [part_number=MG996R]
  F28 = Resettable Fuse PTC [part_number=RKEF075-2 package=ptc]
  J33 = Basic Servo [part_number=LD-20MG]
  F34 = Resettable Fuse PTC [part_number=RKEF075-2 package=ptc]
  J35 = Basic Servo [part_number=LD-20MG]
  F35 = Resettable Fuse PTC [part_number=RKEF075-2 package=ptc]
  D29 = Schottky Diode [part_number=15SQ100 package="300 mil [THT]"]
  D30 = Schottky Diode [part_number=15SQ100 package="300 mil [THT]"]
  Q8 = NPN-Transistor [part_number=BC547CBU-ND package="TO92 [THT]"]
  Q10 = NPN-Transistor [part_number=BC547CBU-ND package="TO92 [THT]"]
  U8 = RELAY [part_number=PR9-5V-200-1A package=relay-g5q]
  U10 = RELAY [part_number=PR9-5V-200-1A package=relay-g5q]

nets:
  I2C_SDA: Brain.A4/SDA, Driver_Limbs.SDA, Driver_Limbs1.SDA
  I2C_SCL: Brain.A5/SCL, Driver_Limbs.SCL, Driver_Limbs1.SCL
  N1: Brain.D8, S4.Pin_4
  N2: Brain.D2, R4.Pin_1
  N3: Brain.D4, Eye_R.IN
  N4: Brain.D7, S3.Pin_4
  Vcc: Brain.5V, Driver_Limbs.VCC, D9.anode, U3.COIL1, D12.anode, U4.COIL1, D16.anode, D17.anode, U5.COIL1, U6.COIL1, Driver_Limbs1.VCC, D26.anode, D27.anode, U8.COIL1, U10.COIL1
  GND: Brain.GND, Driver_Limbs.GND, J2.gnd, J3.gnd, J4.gnd, J5.gnd, J6.gnd, J7.gnd, J8.gnd, J9.gnd, S3.Pin_2, S4.Pin_1, S4.Pin_2, Eye_R.GND, Eye_L.GND, Q3.E, R3.Pin_0, Q4.E, C2.-, PWR_Supply.GND, J15.gnd, J16.gnd, J17.gnd, J18.gnd, J19.gnd, J20.gnd, J21.gnd, J22.gnd, Q5.E, Q6.E, Driver_Limbs1.GND, J24.gnd, J26.gnd, J28.gnd, J33.gnd, J35.gnd, Q8.E, Q10.E
  5V: Brain.VIN, Eye_R.VDD, Eye_L.VDD, U3.MAIN, U4.MAIN, C2.+, PWR_Supply.VCC, U5.MAIN, U6.MAIN, U10.MAIN
  N5: Driver_Limbs.PWM7, J9.pulse
  N6: Driver_Limbs.PWM6, J8.pulse
  N7: Driver_Limbs.PWM5, J7.pulse
  N8: Driver_Limbs.PWM4, J6.pulse
  N9: Driver_Limbs.PWM3, J5.pulse
  N10: Driver_Limbs.PWM2, J4.pulse
  N11: Driver_Limbs.PWM1, J3.pulse
  N12: Driver_Limbs.PWM0, J2.pulse
  N13: Driver_Limbs.PWM15, J22.pulse
  N14: Driver_Limbs.PWM14, J21.pulse
  N15: Driver_Limbs.PWM13, J20.pulse
  N16: Driver_Limbs.PWM12, J19.pulse
  N17: Driver_Limbs.PWM11, J18.pulse
  N18: Driver_Limbs.PWM10, J17.pulse
  N19: Driver_Limbs.PWM9, J16.pulse
  N20: Driver_Limbs.PWM8, J15.pulse
  N21: J2.vcc, F2.2
  N22: F2.1, F3.1, F4.1, F5.1, F6.1, D10.cathode
  N23: J3.vcc, F3.2
  N24: J4.vcc, F4.2
  N25: J5.vcc, F5.2
  N26: J6.vcc, F6.2
  N27: J7.vcc, F7.2
  N28: F7.1, F8.1, F9.1, D13.cathode
  N29: J8.vcc, F8.2
  N30: J9.vcc, F9.2
  N31: Eye_R.OUT, Eye_L.IN
  N32: D8.cathode, D9.cathode
  N33: D8.anode, Q3.C, U3.COIL2
  RelayControl: Q3.B, R3.Pin_1, R4.Pin_0, Q4.B, Q5.B, Q6.B, Q8.B, Q10.B
  N34: U3.NO, D10.anode
  N35: D11.cathode, D12.cathode
  N36: D11.anode, Q4.C, U4.COIL2
  N37: D13.anode, U4.NO
  N38: J15.vcc, F15.2
  N39: F15.1, F16.1, F17.1, F18.1, F19.1, D19.cathode
  N40: D14.cathode, D16.cathode
  N41: D14.anode, Q6.C, U5.COIL2
  N42: D15.cathode, D17.cathode
  N43: D15.anode, Q5.C, U6.COIL2
  N44: J16.vcc, F16.2
  N45: J17.vcc, F17.2
  N46: J18.vcc, F18.2
  N47: J19.vcc, F19.2
  N48: J20.vcc, F20.2
  N49: F20.1, F21.1, F22.1, D18.cathode
  N50: J21.vcc, F21.2
  N51: J22.vcc, F22.2
  N52: D18.anode, U6.NO
  N53: D19.anode, U5.NO
  N54: Driver_Limbs1.PWM4, J35.pulse
  N55: Driver_Limbs1.PWM3, J33.pulse
  N56: Driver_Limbs1.PWM2, J28.pulse
  N57: Driver_Limbs1.PWM1, J26.pulse
  N58: Driver_Limbs1.PWM0, J24.pulse
  N59: J24.vcc, F24.2
  N60: F24.1, F26.1, F28.1, D30.cathode
  N61: D21.cathode, D27.cathode
  N62: D21.anode, Q8.C, U8.COIL2
  N63: D23.cathode, D26.cathode
  N64: D23.anode, Q10.C, U10.COIL2
  N65: J26.vcc, F26.2
  N66: J28.vcc, F28.2
  N67: J33.vcc, F34.2
  N68: F34.1, F35.1, D29.cathode
  N69: J35.vcc, F35.2
  N70: D29.anode, U8.NO
  N71: D30.anode, U10.NO
  7.4V: U8.MAIN

notes:
  Right Side
  Arms
  Legs
  Add a capacitor to spot on driver board with capacitance:
  16V
  1mF
  Input Buttons
  LED Matrix Eyes
  Relays so we don't send power to the motors when we don't need them running. Multiple relays because trying to get relays rated for 20+ A is hard.
  We're using a 12V 30A supply
  Left Side
  Limbs Control
  Neck
  Torso
  Neck/Torso Control
  We need two buck converters. One that goes to 5V, and one that goes to 7.4V, since the torso motors wont drive on 5V
  Buck converters go here
  Still needs the PIR and Ultrasonic added as well
  And possibly the captioning setup

custom parts:
  16-Channel 12-bit PWM Servo Driver - I2C: You want to make a cool robot, maybe a hexapod walker, or maybe just a piece of art with a lot of moving parts. Or maybe you want to drive a lot of LEDs with precise PWM output. Using only two pins, control 16 free-running PWM outputs! You can even chain up 62 breakouts to control up to 992 PWM outputs.
  NeoPixel NeoMatrix 8x8: Put on your sunglasses before wiring up this LED matrix - 64 eye-blistering RGB LEDs adorn the NeoMatrix for a blast of configurable color. Arranged in an 8x8 matrix, each pixel is individually addressable. Only one microcontroller pin is required to control all the LEDs, and you get 24 bit color for each LED.
